# Fritzing sketch circuit_esp32_AMG8833 (saved by Fritzing 1.0.4)
breadboards: 1

parts:
  Componente1 = Adafruit AMG8833 8x8 GRID EYE
  U1 = ESP32S-HiLetgo [part_number=ESP32S-HiLetgo]
  LCD1 = TFT 1.8 inch 160x128 w SD

nets:
  VIN: Componente1.VIN, U1.VIN, LCD1.pin_1
  GND: Componente1.GND, U1.GND, LCD1.pin2

custom parts:
  ESP32S-HiLetgo: HiLetgo ESP-WROOM-32 ESP32 ESP-32S Development Board 2.4GHz Dual-Mode WiFi + Bluetooth Dual Cores Microcontroller The ESP32 integrated with Antenna switches, RF Balun, power amplifiers, low-noise amplifiers, filters, and management modules, and the entire solution occupies the least area of PCB. 2.4 GHz Wi-Fi plus Bluetooth dual-mode chip, with TSMC Ultra-low power consumption 40nm technology,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
  TFT 1.8 inch 160x128 w SD: This is a generic 1.8 tft spi lcd display available on ebay and others. The 1.8" display has 128x160 color pixels.
